// Logisim project Circuito.circ as structural Verilog: 1 circuit, main circuit main
module main (
  input  [3:0] in_1,
  input  [3:0] in_2,
  input  [3:0] in_3,
  input  [3:0] in_4,
  input  [3:0] in_5,
  input  [3:0] in_6,
  input  in_7,
  input  in_8,
  input  in_9,
  input  in_10,
  input  in_11,
  input  in_12,
  input  in_13,
  input  in_14,
  input  [4:0] in_15,
  input  [4:0] in_16,
  input  [3:0] in_17,
  input  [3:0] in_18,
  input  [3:0] in_19,
  input  [3:0] in_20,
  input  [3:0] in_21,
  input  [3:0] in_22,
  output out_23,
  output [3:0] out_24,
  output [3:0] out_25,
  output [3:0] out_26,
  output out_27,
  output out_28,
  output out_29,
  output out_30,
  output out_31,
  output out_32,
  output [4:0] out_33,
  output [4:0] out_34,
  output [3:0] out_35,
  output [3:0] out_36,
  output [3:0] out_37,
  output out_38,
  output out_39,
  output out_40
);

  wire adder_2_cout, adder_3_cout, adder_4_cout, adder_6_cout;

  Hex_Digit_Display hex_digit_display_1 (.value(in_21));  // open: dp
  Hex_Digit_Display hex_digit_display_2 (.value(in_22));  // open: dp
  Adder #(.width(4)) adder_1 (.a(in_5), .b(in_6), .out(out_26), .cout(out_27));  // open: cin
  Adder #(.width(1)) adder_2 (.a(in_7), .b(in_8), .out(out_28), .cout(adder_2_cout));  // open: cin
  Adder #(.width(1)) adder_3 (.a(in_9), .b(in_10), .out(out_29), .cin(adder_2_cout), .cout(adder_3_cout));
  Adder #(.width(1)) adder_4 (.a(in_11), .b(in_12), .out(out_30), .cin(adder_3_cout), .cout(adder_4_cout));
  Adder #(.width(1)) adder_5 (.a(in_13), .b(in_14), .out(out_31), .cin(adder_4_cout), .cout(out_32));
  Negator #(.width(5)) negator_1 (.in(in_16), .out(out_34));
  Subtractor #(.width(4)) subtractor_1 (.a(in_17), .b(in_18), .out(out_35));  // open: bin, bout
  Multiplier #(.width(4)) multiplier_1 (.a(in_19), .b(in_20), .out(out_36), .cout(out_37));  // open: cin
  Comparator #(.width(4)) comparator_1 (.a(in_21), .b(in_22), .gt(out_38), .eq(out_39), .lt(out_40));
  Adder #(.width(4)) adder_6 (.a(in_2), .b(in_4), .out(out_25), .cout(adder_6_cout));  // open: cin
  Adder #(.width(4)) adder_7 (.a(in_1), .b(in_3), .out(out_24), .cin(adder_6_cout), .cout(out_23));
  Adder #(.width(5)) adder_8 (.a(in_15), .b(out_34), .out(out_33));  // open: cin, cout
endmodule
